# Fritzing sketch shutterspeedtester (saved by Fritzing 0.9.4)
breadboards: 1

parts:
  Part1 = Arduino Micro (Rev3)
  Q1 = LTR-301 [package=ltr-301]
  R1 = Resistor [tolerance=±5% resistance=10k package="1206 [SMD]"]
  o1 = Module display OLED I2C 128x64 SSD1306 [package=THT]

nets:
  GND: Part1.GND, R1.Pin_1, o1.GND
  N1: Part1.D2/SDA, o1.SDA
  N2: Part1.D3/SCL, o1.SCL
  N3: Part1.D4_PWM/A6, Q1.E, R1.Pin_0
  5V: Part1.5V, Q1.C, o1.VCC

custom parts:
  Module display OLED I2C 128x64 SSD1306: Ecran OLED I2C SSD163 de 128x64 avec connexion I2C
