# Fritzing sketch shutterspeedtester (saved by Fritzing 0.9.4)
breadboards: 1

parts:
  OLED = Module display OLED I2C 128x64 SSD1306 [package=THT]
  Arduino = seeeduino-xiao
  Phototransistor = LTR-301 [package=ltr-301]
  R1 = Resistor [tolerance=±5% resistance=10k package="1206 [SMD]"]

nets:
  GND: OLED.GND, Arduino.GND, R1.Pin_1
  VCC: OLED.VCC, Arduino.3V3, Phototransistor.C
  N1: OLED.SCL, Arduino.D5
  N2: OLED.SDA, Arduino.D4
  N3: Arduino.D10, Phototransistor.E, R1.Pin_0

custom parts:
  Module display OLED I2C 128x64 SSD1306: Ecran OLED I2C SSD163 de 128x64 avec connexion I2C
  seeeduino-xiao: Seeeduino XIAO processor board.
